# Fritzing sketch L6 Diag (saved by Fritzing 1.0.4)
breadboards: 1

parts:
  Mod1 = MKR ENV Shield
  L298N1 = L298N DC motor driver
  VCC1 = 4 x AAA Battery Mount [internal_resistance=0.1Ω]
  LED1 = LEDs [package=led10mm]
  R1 = Resistor [tolerance=±5% resistance=220 package="1206 [SMD]"]
  M1 = DC Motor [voltage_(max)=6V voltage_(min)=3V]

nets:
  N1: Mod1.D5_PWM, R1.Pin_1
  N2: Mod1.D8_MOSI, L298N1.IN2
  N3: Mod1.D9_SCK, L298N1.IN1
  GND: Mod1.GND, L298N1.GND, VCC1.-, LED1.C
  N4: L298N1.OUT1, M1.pin_2
  N5: L298N1.OUT2, M1.pin_1
  N6: L298N1.5V, VCC1.+
  N7: LED1.A, R1.Pin_0

custom parts:
  MKR ENV Shield: arduino MRK ENV Sheild Atmospheric pressure sensor, temp and humidity, Lux of ambient light, Ultraviolet sensors in MKR form factor.
  L298N DC motor driver: 2x DC motor driver with 78M05 positive voltage regulator (7..35 V) L298N: max 46 V, 2 A Set 5 V Enable jumper to enable 5 V regultor (needed for the L298N) and +5 V output at screw terminal or supply external +5 V at screw terminal Set ENA and/or ENB to +5 V to enable motor permanently or supply ENA and/or ENB with PWM signal IN1 and IN2 set rotation directory for motor A (OUT1/OUT2) IN2 and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
