# Fritzing sketch L6 Diag_LED (saved by Fritzing 1.0.4)
breadboards: 1

parts:
  Mod1 = MKR ENV Shield
  LED1 = LEDs [package=led10mm]
  R1 = Resistor [tolerance=±5% resistance=220 package="1206 [SMD]"]

nets:
  N1: Mod1.D5_PWM, R1.Pin_1
  N2: Mod1.GND, LED1.C
  N3: LED1.A, R1.Pin_0

custom parts:
  MKR ENV Shield: arduino MRK ENV Sheild Atmospheric pressure sensor, temp and humidity, Lux of ambient light, Ultraviolet sensors in MKR form factor.
