# Fritzing sketch LED diagram (saved by Fritzing 0.9.4)
breadboards: 1

parts:
  Part1 = Arduino MKR1000
  R1 = Resistor [tolerance=±5% resistance=220 package="0603 [SMD]"]
  LED1 = LED - 5mm [color="White (8000K)" package="5 mm [THT]"]

nets:
  N1: Part1.D5_PWM, R1.Pin_0
  N2: Part1.GND, LED1.cathode
  N3: R1.Pin_1, LED1.anode

custom parts:
  Arduino MKR1000: MKR1000 is a powerful board that combines the functionality of the Zero and the Wi-Fi Shield. It is the ideal solution for makers wanting to design IoT projects with minimal previous experience in networking
