# Fritzing sketch LCD Screen (saved by Fritzing 0.9.4)
breadboards: 1

parts:
  LCD1 = LCD screen
  U1 = POT [package=pot_alpha_rv16af-20]
  Part4 = Arduino MKR1000

nets:
  VSS: LCD1.VSS, LCD1.R/W, LCD1.LED-, U1.A, Part4.GND
  VDD: LCD1.VDD, LCD1.LED+, U1.E, Part4.5V
  N1: LCD1.V0, U1.S
  N2: LCD1.RS, Part4.D12_SCL
  N3: LCD1.E, Part4.D11_SDA
  N4: LCD1.DB4, Part4.D5_PWM
  N5: LCD1.DB5, Part4.D4_PWM
  N6: LCD1.DB6, Part4.D3_PWM
  N7: LCD1.DB7, Part4.D2_PWM

custom parts:
  Arduino MKR1000: MKR1000 is a powerful board that combines the functionality of the Zero and the Wi-Fi Shield. It is the ideal solution for makers wanting to design IoT projects with minimal previous experience in networking
