# Fritzing sketch Lock Box With Resistors (saved by Fritzing 0.9.4)
breadboards: 1

parts:
  Part1 = Arduino Uno (Rev3)
  LED2 = smd LED [color="Red (633nm)" package="1206 [SMD]"]
  S1 = Momentary Switch [package=ksa_sealed_tac_switch]
  J1 = Basic Servo
  LED3 = smd LED [color="Red (633nm)" package="1206 [SMD]"]
  S2 = Momentary Switch [package=ksa_sealed_tac_switch]
  LED4 = smd LED [color="Red (633nm)" package="1206 [SMD]"]
  S3 = Momentary Switch [package=ksa_sealed_tac_switch]
  LED5 = smd LED [color="Red (633nm)" package="1206 [SMD]"]
  S4 = Momentary Switch [package=ksa_sealed_tac_switch]
  LED6 = smd LED [color="Green (555nm)" package="1206 [SMD]"]
  R1 = Resistor [tolerance=±5% resistance=220 package=THT]
  R2 = Resistor [tolerance=±5% resistance=220 package=THT]
  R3 = Resistor [tolerance=±5% resistance=220 package=THT]
  R4 = Resistor [tolerance=±5% resistance=220 package=THT]
  R5 = Resistor [tolerance=±5% resistance=220 package=THT]

nets:
  N1: Part1.A0, LED2.anode, R2.Pin_0, R2.Pin_1
  N2: Part1.A1, LED4.anode, R1.Pin_0, R1.Pin_1
  N3: Part1.A3, LED5.anode, R4.Pin_0, R4.Pin_1
  N4: Part1.A4/SDA, LED3.anode, R5.Pin_0, R5.Pin_1
  N5: Part1.D9_PWM, LED6.anode, R3.Pin_0, R3.Pin_1
  GND: Part1.GND, LED2.cathode, S1.3, S1.4, J1.gnd, LED3.cathode, S2.3, S2.4
  N6: Part1.D2, S4.1, S4.2
  N7: Part1.D3_PWM, S1.1, S1.2
  N8: Part1.D4, J1.pulse
  N9: Part1.D5_PWM, S3.1, S3.2
  N10: Part1.D6_PWM, S2.1, S2.2
  5V: Part1.5V, J1.vcc
  N11: LED4.cathode, S3.3, S3.4, LED5.cathode, S4.3, S4.4, LED6.cathode
